# Fritzing sketch IR (saved by Fritzing 0.9.3b)
breadboards: 1

parts:
  Part1 = Arduino Mega 2560 (Rev3)
  IR1 = TSOP312.., 314.. [package=THT]  # not connected
  LED1 = smd LED [color="Red (633nm)" package="0805 [SMD]"]
  R1 = Resistor [tolerance=±5% resistance=330 package="2010 [SMD]"]

nets:
  N1: Part1.GND, LED1.cathode
  N2: Part1.D52, R1.Pin_1
  N3: LED1.anode, R1.Pin_0
